# Fritzing sketch iot_sample_components (saved by Fritzing 0.9.3b)
breadboards: 1

parts:
  photo = PHOTOCELL [package=photocell-kit]
  R1 = Resistor [tolerance=±5% resistance=220 package=THT]

nets:
  5V: photo.P$1
  N1: photo.P$2, R1.Pin_0
  GND: R1.Pin_1

notes:
  pin
